// Digital circuit 2-to-1_selector.dig as structural Verilog
module _2_to_1_selector (
  input  B,
  input  A,
  input  Select,
  output Out
);

  wire and_1_out, and_2_out, not_1_out;

  not not_1 (not_1_out, Select);
  and and_1 (and_1_out, B, Select);
  and and_2 (and_2_out, A, not_1_out);
  or or_1 (Out, and_1_out, and_2_out);
endmodule
