// Digital circuit 8-bit-latch-simple.dig as structural Verilog
module _8_bit_latch_simple (
  input  [7:0] D,
  input  Clock,
  output [7:0] _8
);

  level_triggered_d_type_flip_flop level_triggered_d_type_flip_flop_1 (.Data(D[0]), .Clock(Clock), .Q(_8[0]));
  level_triggered_d_type_flip_flop level_triggered_d_type_flip_flop_2 (.Data(D[1]), .Clock(Clock), .Q(_8[1]));
  level_triggered_d_type_flip_flop level_triggered_d_type_flip_flop_3 (.Data(D[2]), .Clock(Clock), .Q(_8[2]));
  level_triggered_d_type_flip_flop level_triggered_d_type_flip_flop_4 (.Data(D[3]), .Clock(Clock), .Q(_8[3]));
  level_triggered_d_type_flip_flop level_triggered_d_type_flip_flop_5 (.Data(D[4]), .Clock(Clock), .Q(_8[4]));
  level_triggered_d_type_flip_flop level_triggered_d_type_flip_flop_6 (.Data(D[5]), .Clock(Clock), .Q(_8[5]));
  level_triggered_d_type_flip_flop level_triggered_d_type_flip_flop_7 (.Data(D[6]), .Clock(Clock), .Q(_8[6]));
  level_triggered_d_type_flip_flop level_triggered_d_type_flip_flop_8 (.Data(D[7]), .Clock(Clock), .Q(_8[7]));
endmodule
