// Digital circuit eight_bit_adder.dig as structural Verilog
module eight_bit_adder (
  output out_1,
  output out_2,
  output out_3,
  output out_4,
  output out_5
);

  wire add_2_c_o, add_3_c_o, add_4_c_o, dipswitch_1_out, dipswitch_2_out, dipswitch_3_out, dipswitch_4_out,
       dipswitch_5_out, dipswitch_6_out, dipswitch_7_out, dipswitch_8_out, dipswitch_9_out;

  DipSwitch dipswitch_1 (.out(dipswitch_1_out));
  DipSwitch dipswitch_2 (.out(dipswitch_2_out));
  DipSwitch dipswitch_3 (.out(dipswitch_3_out));
  DipSwitch dipswitch_4 (.out(dipswitch_4_out));
  DipSwitch dipswitch_5 (.out(dipswitch_5_out));
  DipSwitch dipswitch_6 (.out(dipswitch_6_out));
  DipSwitch dipswitch_7 (.out(dipswitch_7_out));
  DipSwitch dipswitch_8 (.out(dipswitch_8_out));
  DipSwitch dipswitch_9 (.out(dipswitch_9_out));
  Add add_1 (.a(dipswitch_5_out), .b(dipswitch_1_out), .c_i(add_2_c_o), .s(out_2), .c_o(out_1));
  Add add_2 (.a(dipswitch_6_out), .b(dipswitch_2_out), .c_i(add_3_c_o), .s(out_3), .c_o(add_2_c_o));
  Add add_3 (.a(dipswitch_7_out), .b(dipswitch_3_out), .c_i(add_4_c_o), .s(out_4), .c_o(add_3_c_o));
  Add add_4 (.a(dipswitch_8_out), .b(dipswitch_4_out), .c_i(dipswitch_9_out), .s(out_5), .c_o(add_4_c_o));
endmodule
