// Digital circuit edge_trigger_d-type_flip-flop.dig as structural Verilog
module edge_trigger_d_type_flip_flop (
  input  Clear,
  input  Preset,
  input  D,
  input  Clock,
  output Q,
  output Q_Bar
);

  wire nor_1_out, nor_2_out, nor_3_out, nor_4_out, not_1_out;

  not not_1 (not_1_out, Clock);
  nor nor_1 (nor_1_out, Clear, nor_4_out, nor_2_out);
  nor nor_2 (nor_2_out, nor_1_out, Preset, not_1_out);
  nor nor_3 (nor_3_out, nor_2_out, not_1_out, nor_4_out);
  nor nor_4 (nor_4_out, nor_3_out, Preset, D);
  nor nor_5 (Q_Bar, Q, Preset, nor_3_out);
  nor nor_6 (Q, Clear, nor_2_out, Q_Bar);
endmodule
