// Digital circuit eight_bit_adder.dig as structural Verilog
module eight_bit_adder (
  input  [7:0] A,
  input  [7:0] B,
  input  Ci,
  output Co,
  output [7:0] D
);

  wire add_2_c_o, add_3_c_o, add_4_c_o, add_5_c_o, add_6_c_o, add_7_c_o, add_8_c_o;

  Add add_1 (.a(A[7]), .b(B[7]), .c_i(add_2_c_o), .s(D[7]), .c_o(Co));
  Add add_2 (.a(A[6]), .b(B[6]), .c_i(add_3_c_o), .s(D[6]), .c_o(add_2_c_o));
  Add add_3 (.a(A[5]), .b(B[5]), .c_i(add_4_c_o), .s(D[5]), .c_o(add_3_c_o));
  Add add_4 (.a(A[4]), .b(B[4]), .c_i(add_5_c_o), .s(D[4]), .c_o(add_4_c_o));
  Add add_5 (.a(A[3]), .b(B[3]), .c_i(add_6_c_o), .s(D[3]), .c_o(add_5_c_o));
  Add add_6 (.a(A[2]), .b(B[2]), .c_i(add_7_c_o), .s(D[2]), .c_o(add_6_c_o));
  Add add_7 (.a(A[1]), .b(B[1]), .c_i(add_8_c_o), .s(D[1]), .c_o(add_7_c_o));
  Add add_8 (.a(A[0]), .b(B[0]), .c_i(Ci), .s(D[0]), .c_o(add_8_c_o));
endmodule
