// Digital circuit ripple_counter.dig as structural Verilog
module ripple_counter (
  input  clk,
  input  in_2,
  input  in_3
);

  wire jk_ff_as_1_q, jk_ff_as_2_q, jk_ff_as_3_q, jk_ff_as_4_q, jk_ff_as_5_q, jk_ff_as_6_q, jk_ff_as_7_q,
       jk_ff_as_8_q;

  LED led_1 (.in(jk_ff_as_8_q));
  LED led_2 (.in(jk_ff_as_7_q));
  LED led_3 (.in(jk_ff_as_6_q));
  LED led_4 (.in(jk_ff_as_5_q));
  LED led_5 (.in(jk_ff_as_4_q));
  LED led_6 (.in(jk_ff_as_3_q));
  LED led_7 (.in(jk_ff_as_2_q));
  LED led_8 (.in(jk_ff_as_1_q));
  JK_FF_AS jk_ff_as_1 (.Set(in_3), .J(in_2), .C(clk), .K(in_2), .Clr(in_3), .Q(jk_ff_as_1_q));  // open: nQ
  JK_FF_AS jk_ff_as_2 (.Set(in_3), .J(in_2), .C(jk_ff_as_1_q), .K(in_2), .Clr(in_3), .Q(jk_ff_as_2_q));  // open: nQ
  JK_FF_AS jk_ff_as_3 (.Set(in_3), .J(in_2), .C(jk_ff_as_2_q), .K(in_2), .Clr(in_3), .Q(jk_ff_as_3_q));  // open: nQ
  JK_FF_AS jk_ff_as_4 (.Set(in_3), .J(in_2), .C(jk_ff_as_3_q), .K(in_2), .Clr(in_3), .Q(jk_ff_as_4_q));  // open: nQ
  JK_FF_AS jk_ff_as_5 (.Set(in_3), .J(in_2), .C(jk_ff_as_4_q), .K(in_2), .Clr(in_3), .Q(jk_ff_as_5_q));  // open: nQ
  JK_FF_AS jk_ff_as_6 (.Set(in_3), .J(in_2), .C(jk_ff_as_5_q), .K(in_2), .Clr(in_3), .Q(jk_ff_as_6_q));  // open: nQ
  JK_FF_AS jk_ff_as_7 (.Set(in_3), .J(in_2), .C(jk_ff_as_6_q), .K(in_2), .Clr(in_3), .Q(jk_ff_as_7_q));  // open: nQ
  JK_FF_AS jk_ff_as_8 (.Set(in_3), .J(in_2), .C(jk_ff_as_7_q), .K(in_2), .Clr(in_3), .Q(jk_ff_as_8_q));  // open: nQ

  // Notes on the sheet:
  //   clk: Hz: 5
endmodule
