// Digital circuit test.dig as structural Verilog
module test (
  input  in_1,
  input  in_2,
  input  in_3,
  output out_4
);

  _2_to_1_selector _2_to_1_selector_1 (.B(in_1), .A(in_2), .Select(in_3), .Out(out_4));
endmodule
