// Digital circuit 4_bit_adder.dig as structural Verilog
module _4_bit_adder (
  output out_1,
  output out_2,
  output out_3,
  output out_4,
  output out_5,
  output out_6,
  output out_7,
  output out_8,
  output out_9
);

  wire add_1_c_o, add_2_c_o, add_3_c_o, add_4_c_o, add_5_c_o, add_6_c_o, add_7_c_o, add_8_c_o,
       dipswitch_1_out, dipswitch_2_out, dipswitch_3_out, dipswitch_4_out, dipswitch_5_out, dipswitch_6_out,
       dipswitch_7_out, dipswitch_8_out, dipswitch_9_out, dipswitch_10_out, dipswitch_11_out,
       dipswitch_12_out, dipswitch_13_out, dipswitch_14_out, dipswitch_15_out, dipswitch_16_out,
       dipswitch_17_out, dipswitch_18_out, dipswitch_19_out, xor_1_out, xor_2_out, xor_3_out, xor_4_out,
       xor_5_out, xor_6_out, xor_7_out, xor_8_out;

  DipSwitch dipswitch_1 (.out(dipswitch_1_out));
  DipSwitch dipswitch_2 (.out(dipswitch_2_out));
  DipSwitch dipswitch_3 (.out(dipswitch_3_out));
  DipSwitch dipswitch_4 (.out(dipswitch_4_out));
  DipSwitch dipswitch_5 (.out(dipswitch_5_out));
  DipSwitch dipswitch_6 (.out(dipswitch_6_out));
  DipSwitch dipswitch_7 (.out(dipswitch_7_out));
  DipSwitch dipswitch_8 (.out(dipswitch_8_out));
  DipSwitch dipswitch_9 (.out(dipswitch_9_out));
  DipSwitch dipswitch_10 (.out(dipswitch_10_out));
  DipSwitch dipswitch_11 (.out(dipswitch_11_out));
  DipSwitch dipswitch_12 (.out(dipswitch_12_out));
  DipSwitch dipswitch_13 (.out(dipswitch_13_out));
  DipSwitch dipswitch_14 (.out(dipswitch_14_out));
  DipSwitch dipswitch_15 (.out(dipswitch_15_out));
  DipSwitch dipswitch_16 (.out(dipswitch_16_out));
  xor xor_1 (xor_1_out, dipswitch_9_out, dipswitch_17_out);
  xor xor_2 (xor_2_out, dipswitch_10_out, dipswitch_17_out);
  xor xor_3 (xor_3_out, dipswitch_11_out, dipswitch_17_out);
  xor xor_4 (xor_4_out, dipswitch_12_out, dipswitch_17_out);
  xor xor_5 (xor_5_out, dipswitch_13_out, dipswitch_17_out);
  xor xor_6 (xor_6_out, dipswitch_14_out, dipswitch_17_out);
  xor xor_7 (xor_7_out, dipswitch_15_out, dipswitch_17_out);
  xor xor_8 (xor_8_out, dipswitch_16_out, dipswitch_17_out);
  DipSwitch dipswitch_17 (.out(dipswitch_17_out));
  Add add_1 (.a(dipswitch_1_out), .b(xor_1_out), .c_i(add_2_c_o), .s(out_6), .c_o(add_1_c_o));
  Add add_2 (.a(dipswitch_2_out), .b(xor_2_out), .c_i(add_3_c_o), .s(out_7), .c_o(add_2_c_o));
  Add add_3 (.a(dipswitch_3_out), .b(xor_3_out), .c_i(add_4_c_o), .s(out_8), .c_o(add_3_c_o));
  Add add_4 (.a(dipswitch_4_out), .b(xor_4_out), .c_i(add_5_c_o), .s(out_9), .c_o(add_4_c_o));
  Add add_5 (.a(dipswitch_5_out), .b(xor_5_out), .c_i(add_6_c_o), .s(out_2), .c_o(add_5_c_o));
  Add add_6 (.a(dipswitch_6_out), .b(xor_6_out), .c_i(add_7_c_o), .s(out_3), .c_o(add_6_c_o));
  Add add_7 (.a(dipswitch_7_out), .b(xor_7_out), .c_i(add_8_c_o), .s(out_4), .c_o(add_7_c_o));
  Add add_8 (.a(dipswitch_8_out), .b(xor_8_out), .c_i(dipswitch_18_out), .s(out_5), .c_o(add_8_c_o));
  DipSwitch dipswitch_18 (.out(dipswitch_18_out));
  DipSwitch dipswitch_19 (.out(dipswitch_19_out));
  xor xor_9 (out_1, dipswitch_19_out, add_1_c_o);
endmodule
