// Digital circuit 8-bit-latch.dig as structural Verilog
module _8_bit_latch (
  input  Clock,
  input  [7:0] _8_Bit_Data,
  output [7:0] _8_Bit_Q
);

  wire and_1_out, and_2_out, and_3_out, and_4_out, and_5_out, and_6_out, and_7_out, and_8_out, and_9_out,
       and_10_out, and_11_out, and_12_out, and_13_out, and_14_out, and_15_out, and_16_out, nor_2_out,
       nor_4_out, nor_6_out, nor_8_out, nor_10_out, nor_12_out, nor_14_out, nor_16_out, not_1_out, not_2_out,
       not_3_out, not_4_out, not_5_out, not_6_out, not_7_out, not_8_out;

  not not_1 (not_1_out, _8_Bit_Data[0]);
  not not_2 (not_2_out, _8_Bit_Data[1]);
  not not_3 (not_3_out, _8_Bit_Data[2]);
  not not_4 (not_4_out, _8_Bit_Data[3]);
  not not_5 (not_5_out, _8_Bit_Data[4]);
  not not_6 (not_6_out, _8_Bit_Data[5]);
  not not_7 (not_7_out, _8_Bit_Data[6]);
  not not_8 (not_8_out, _8_Bit_Data[7]);
  and and_1 (and_1_out, not_1_out, Clock);
  and and_2 (and_2_out, Clock, _8_Bit_Data[0]);
  and and_3 (and_3_out, not_2_out, Clock);
  and and_4 (and_4_out, Clock, _8_Bit_Data[1]);
  and and_5 (and_5_out, not_3_out, Clock);
  and and_6 (and_6_out, Clock, _8_Bit_Data[2]);
  and and_7 (and_7_out, not_4_out, Clock);
  and and_8 (and_8_out, Clock, _8_Bit_Data[3]);
  and and_9 (and_9_out, not_5_out, Clock);
  and and_10 (and_10_out, Clock, _8_Bit_Data[4]);
  and and_11 (and_11_out, not_6_out, Clock);
  and and_12 (and_12_out, Clock, _8_Bit_Data[5]);
  and and_13 (and_13_out, not_7_out, Clock);
  and and_14 (and_14_out, Clock, _8_Bit_Data[6]);
  and and_15 (and_15_out, not_8_out, Clock);
  and and_16 (and_16_out, Clock, _8_Bit_Data[7]);
  nor nor_1 (_8_Bit_Q[0], and_1_out, nor_2_out);
  nor nor_2 (nor_2_out, _8_Bit_Q[0], and_2_out);
  nor nor_3 (_8_Bit_Q[1], and_3_out, nor_4_out);
  nor nor_4 (nor_4_out, _8_Bit_Q[1], and_4_out);
  nor nor_5 (_8_Bit_Q[2], and_5_out, nor_6_out);
  nor nor_6 (nor_6_out, _8_Bit_Q[2], and_6_out);
  nor nor_7 (_8_Bit_Q[3], and_7_out, nor_8_out);
  nor nor_8 (nor_8_out, _8_Bit_Q[3], and_8_out);
  nor nor_9 (_8_Bit_Q[4], and_9_out, nor_10_out);
  nor nor_10 (nor_10_out, _8_Bit_Q[4], and_10_out);
  nor nor_11 (_8_Bit_Q[5], and_11_out, nor_12_out);
  nor nor_12 (nor_12_out, _8_Bit_Q[5], and_12_out);
  nor nor_13 (_8_Bit_Q[6], and_13_out, nor_14_out);
  nor nor_14 (nor_14_out, _8_Bit_Q[6], and_14_out);
  nor nor_15 (_8_Bit_Q[7], and_15_out, nor_16_out);
  nor nor_16 (nor_16_out, _8_Bit_Q[7], and_16_out);
endmodule
