// Digital circuit 8-bit_2-to-1_selector.dig as structural Verilog
module _8_bit_2_to_1_selector (
  input  [7:0] A,
  input  [7:0] B,
  input  Select,
  output [7:0] Out
);

  _2_to_1_selector _2_to_1_selector_1 (.B(B[0]), .A(A[0]), .Select(Select), .Out(Out[0]));
  _2_to_1_selector _2_to_1_selector_2 (.B(B[1]), .A(A[1]), .Select(Select), .Out(Out[1]));
  _2_to_1_selector _2_to_1_selector_3 (.B(B[2]), .A(A[2]), .Select(Select), .Out(Out[2]));
  _2_to_1_selector _2_to_1_selector_4 (.B(A[3]), .A(A[3]), .Select(Select), .Out(Out[3]));
  _2_to_1_selector _2_to_1_selector_5 (.B(B[4]), .A(A[4]), .Select(Select), .Out(Out[4]));
  _2_to_1_selector _2_to_1_selector_6 (.B(B[5]), .A(A[5]), .Select(Select), .Out(Out[5]));
  _2_to_1_selector _2_to_1_selector_7 (.B(B[6]), .A(A[6]), .Select(Select), .Out(Out[6]));
  _2_to_1_selector _2_to_1_selector_8 (.B(B[7]), .A(A[7]), .Select(Select), .Out(Out[7]));

  assign B[3] = A[3];
endmodule
