// Digital circuit level-triggered d-type flip-flop.dig as structural Verilog
module level_triggered_d_type_flip_flop (
  input  Data,
  input  Clock
);

  wire and_1_out, and_2_out, nor_1_out, nor_2_out, not_1_out;

  not not_1 (not_1_out, Data);
  and and_1 (and_1_out, not_1_out, Clock);
  and and_2 (and_2_out, Clock, Data);
  nor nor_1 (nor_1_out, and_1_out, nor_2_out);
  nor nor_2 (nor_2_out, nor_1_out, and_2_out);
  LED Q (.in(nor_1_out));
  LED Q_Bar (.in(nor_2_out));
endmodule
